# Fritzing sketch breadboard_schematic (saved by Fritzing 0.9.3b)
breadboards: 1

parts:
  LED1 = RGB LED (com. anode, rbg) [package="5 mm [THT]"]
  Componente2 = BluePill
  J1 = Basic Servo
  SW1 = DIP Switch 4 Position [package=dipswitch-04]

nets:
  N1: LED1.red_cathode, Componente2.B15
  GND3: LED1.common_anode, Componente2.GND3, J1.gnd, SW1.2, SW1.3, SW1.4
  N2: LED1.blue_cathode, Componente2.B14
  N3: LED1.green_cathode, Componente2.B13
  N4: Componente2.A4, SW1.7
  N5: Componente2.A5, SW1.6
  N6: Componente2.A6, SW1.5
  5V: Componente2.5V, J1.vcc
  N7: Componente2.A8, J1.pulse
